// Logisim project RISC-V.circ as structural Verilog: 7 circuits, main circuit main
module main (
);

  wire and_1_out, AUIPC, branch_evaluator_out_4, clock_1_out, comparator_1_eq, comparator_2_eq, JAL, JALR,
       LUI, not_1_out, not_2_out, not_3_out, not_4_out, or_1_out, or_2_out;
  wire [2:0] funct3;
  wire [4:0] immediate_decoder_1_rd, immediate_decoder_1_rs1, immediate_decoder_1_rs2, multiplexer_1_out,
       multiplexer_2_out;
  wire [6:0] funct7, opcode;
  wire [11:0] immediate_decoder_1_i;
  wire [19:0] immediate_decoder_1_u;
  wire [23:0] adder_3_out_2, bit_extender_2_out, counter_1_q;
  wire [31:0] adder_1_out, adder_2_out, adder_3_out, ALU_out_5, bit_extender_1_out, multiplexer_3_out,
       multiplexer_4_out, multiplexer_5_out, multiplexer_6_out, multiplexer_7_out, ram_1_data, ram_2_data,
       register_1_q, register_2_q, rom_1_data;

  Clock clock_1 (.out(clock_1_out));
  and and_1 (and_1_out, clock_1_out, not_2_out);
  not not_1 (not_1_out, clock_1_out);
  not not_2 (not_2_out, not_1_out);
  immediate_chooser immediate_chooser_1 (.opcode(opcode), .funct3(funct3));  // open: I, R, S, B, U, J
  Counter #(.width(24), .max('hffffff), .trigger("falling")) counter_1 (
    .load(or_1_out), .D(adder_3_out_2), .count(not_3_out), .Q(counter_1_q), .clk(and_1_out));  // open: carry, clr
  not not_3 (not_3_out, or_1_out);
  buf or_1 (or_1_out, JALR);  // OR_Gate
  not not_4 (not_4_out, clock_1_out);
  LUI_AUIPC_JAL_JALR lui_auipc_jal_jalr_1 (.in_1(opcode), .JALR(JALR), .JAL(JAL), .AUIPC(AUIPC), .LUI(LUI));
  ROM #(.addrWidth(24), .dataWidth(32)) rom_1 (.addr(counter_1_q), .data(rom_1_data));  // open: sel
  immediate_decoder immediate_decoder_1 (
    .in_1(rom_1_data), .rd(immediate_decoder_1_rd), .rs1(immediate_decoder_1_rs1),
    .rs2(immediate_decoder_1_rs2), .funct3(funct3), .funct7(funct7), .I(immediate_decoder_1_i),
    .U(immediate_decoder_1_u), .opcode(opcode));  // open: S, B, J
  assign bit_extender_1_out = {{20{immediate_decoder_1_i[11]}}, immediate_decoder_1_i};  // Bit_Extender bit_extender_1
  Adder #(.width(32)) adder_1 (
    .a({immediate_decoder_1_u, {12{1'b0}}}), .b({{6{1'b0}}, counter_1_q, 2'b00}), .out(adder_1_out));  // open: cin, cout
  Adder #(.width(32)) adder_2 (.a({{6{1'b0}}, counter_1_q, 2'b00}), .b(32'h4), .out(adder_2_out));  // open: cin, cout
  Adder #(.width(32)) adder_3 (
    .a(register_1_q), .b(bit_extender_1_out), .out({adder_3_out[31:26], adder_3_out_2, adder_3_out[1:0]}));  // open: cin, cout
  Multiplexer #(.width(5)) multiplexer_1 (
    .in0(immediate_decoder_1_rs1), .in1(immediate_decoder_1_rd), .out(multiplexer_1_out), .sel(and_1_out));  // open: en
  Multiplexer #(.width(5)) multiplexer_2 (
    .in0(immediate_decoder_1_rs2), .in1(immediate_decoder_1_rd), .out(multiplexer_2_out), .sel(and_1_out));  // open: en
  Multiplexer #(.width(32)) multiplexer_3 (
    .in0(multiplexer_4_out), .in1({immediate_decoder_1_u, {12{1'b0}}}), .out(multiplexer_3_out), .sel(LUI));  // open: en
  Multiplexer #(.width(32)) multiplexer_4 (
    .in0(multiplexer_5_out), .in1(adder_1_out), .out(multiplexer_4_out), .sel(AUIPC));  // open: en
  Multiplexer #(.width(32)) multiplexer_5 (
    .in0(ALU_out_5), .in1(adder_2_out), .out(multiplexer_5_out), .sel(or_2_out));  // open: en
  Comparator #(.width(5), .mode("unsigned")) comparator_1 (
    .a({5{1'b0}}), .b(multiplexer_1_out), .eq(comparator_1_eq));  // open: gt, lt
  Comparator #(.width(5), .mode("unsigned")) comparator_2 (
    .a({5{1'b0}}), .b(multiplexer_2_out), .eq(comparator_2_eq));  // open: gt, lt
  or or_2 (or_2_out, JAL, JALR);
  RAM #(.addrWidth(5), .dataWidth(32), .bus("separate")) ram_1 (
    .addr(multiplexer_1_out), .din(multiplexer_3_out), .data(ram_1_data), .clk(and_1_out), .ld(1'b1));  // open: str, sel, clr
  RAM #(.addrWidth(5), .dataWidth(32), .bus("separate")) ram_2 (
    .addr(multiplexer_2_out), .din(multiplexer_3_out), .data(ram_2_data), .clk(and_1_out), .ld(1'b1));  // open: str, sel, clr
  Bit_Extender #(.in_width(32), .out_width(24)) bit_extender_2 (.out(bit_extender_2_out));  // open: in
  Multiplexer #(.width(32)) multiplexer_6 (
    .in0(ram_1_data), .in1({32{1'b0}}), .out(multiplexer_6_out), .sel(comparator_1_eq));  // open: en
  Multiplexer #(.width(32)) multiplexer_7 (
    .in0(ram_2_data), .in1({32{1'b0}}), .out(multiplexer_7_out), .sel(comparator_2_eq));  // open: en
  Register #(.width(32), .trigger("high")) register_1 (
    .D(multiplexer_6_out), .Q(register_1_q), .clk(not_4_out));  // open: en, clr
  Register #(.width(32), .trigger("high")) register_2 (
    .D(multiplexer_7_out), .Q(register_2_q), .clk(not_4_out));  // open: en, clr
  RAM #(.addrWidth(24), .dataWidth(32), .bus("separate")) ram_3 (.addr(bit_extender_2_out));  // open: din, data, str, sel, clk, ld, clr
  ALU ALU (.rs1(register_1_q), .rs2(register_2_q), .funct7_i_think(funct7), .funct3(funct3), .out_5(ALU_out_5));
  branch_evaluator branch_evaluator (
    .rs1(register_1_q), .rs2(register_2_q), .funct3(funct3), .out_4(branch_evaluator_out_4));

  // Notes on the sheet:
  //   splitter discards 2 least significant and 6 most significant bits
  //   control state B
  //   branch evaluator output
  //   control state A
  //   add 2 bits on the bottom, and 6 on the top
  //   rs1 + sign extended I-immediate for JALR instruction
  //   no need to set LSB to zero as bottom 2 bits will be discarded anyway
  //   todo this needs delay
  //   JAL and JALR both write PC+4 to rd
  //   rs1 line to to add to sign extended I-immediate for JALR instruction
endmodule

module immediate_decoder (
  input  [31:0] in_1,
  output [4:0] rd,
  output [4:0] rs1,
  output [6:0] opcode,
  output [4:0] rs2,
  output [2:0] funct3,
  output [6:0] funct7,
  output [11:0] I,
  output [11:0] S,
  output [12:0] B,
  output [19:0] U,
  output [31:0] J
);

  assign J = {{11{in_1[31]}}, {in_1[31], in_1[19:12], in_1[20], in_1[30:21], 1'b0}};  // Bit_Extender bit_extender_1

  assign B = {in_1[31], in_1[7], in_1[30:25], in_1[11:8], 1'b0};
  assign funct3 = in_1[14:12];
  assign funct7 = in_1[31:25];
  assign I = in_1[31:20];
  assign opcode = in_1[6:0];
  assign rd = in_1[11:7];
  assign rs1 = in_1[19:15];
  assign rs2 = in_1[24:20];
  assign S = {in_1[31:25], in_1[11:7]};
  assign U = in_1[31:12];
endmodule

module jump_evaluator (
  input  [23:0] current_program_counter,
  input  [31:0] relative_J_immediate,
  input  ALU_conditional,
  output [23:0] next_program_counter_value
);
endmodule

module ALU (
  input  [6:0] funct7_i_think,
  input  [31:0] rs1,
  input  [31:0] rs2,
  input  [2:0] funct3,
  output [31:0] out_5
);

  wire comparator_1_gt, comparator_2_gt;
  wire [31:0] adder_1_out, and_1_out, bit_extender_1_out, bit_extender_2_out, multiplexer_1_out,
       multiplexer_2_out, or_1_out, shifter_1_out, shifter_2_out, shifter_3_out, subtractor_1_out, xor_1_out;

  Adder #(.width(32)) adder_1 (.a(rs2), .b(rs1), .out(adder_1_out));  // open: cin, cout
  Subtractor #(.width(32)) subtractor_1 (.a(rs2), .b(rs1), .out(subtractor_1_out));  // open: bin, bout
  Shifter #(.width(32)) shifter_1 (.in(rs2), .\dist (rs1[4:0]), .out(shifter_1_out));
  Comparator #(.width(32)) comparator_1 (.a(rs2), .b(rs1), .gt(comparator_1_gt));  // open: eq, lt
  Comparator #(.width(32), .mode("unsigned")) comparator_2 (.a(rs2), .b(rs1), .gt(comparator_2_gt));  // open: eq, lt
  Shifter #(.width(32), .shift("lr")) shifter_2 (.in(rs2), .\dist (rs1[4:0]), .out(shifter_2_out));
  Shifter #(.width(32), .shift("ar")) shifter_3 (.in(rs2), .\dist (rs1[4:0]), .out(shifter_3_out));
  Multiplexer #(.width(32)) multiplexer_1 (
    .in0(adder_1_out), .in1(subtractor_1_out), .out(multiplexer_1_out), .sel(funct7_i_think[5]));  // open: en
  assign xor_1_out = rs2 ^ rs1;  // XOR_Gate xor_1, 32 bits wide
  Multiplexer #(.width(32)) multiplexer_2 (
    .in0(shifter_2_out), .in1(shifter_3_out), .out(multiplexer_2_out), .sel(funct7_i_think[5]));  // open: en
  assign or_1_out = rs2 | rs1;  // OR_Gate or_1, 32 bits wide
  assign and_1_out = rs2 & rs1;  // AND_Gate and_1, 32 bits wide
  assign bit_extender_1_out = {{31{1'b0}}, comparator_1_gt};  // Bit_Extender bit_extender_1
  assign bit_extender_2_out = {{31{1'b0}}, comparator_2_gt};  // Bit_Extender bit_extender_2
  Multiplexer #(.select(3), .width(32)) multiplexer_3 (
    .in0(multiplexer_1_out), .in1(shifter_1_out), .in2(bit_extender_1_out), .in3(bit_extender_2_out),
    .in4(xor_1_out), .in5(multiplexer_2_out), .in6(or_1_out), .in7(and_1_out), .out(out_5), .sel(funct3));  // open: en

  // Notes on the sheet:
  //   ADD
  //   SUB
  //   SLL
  //   SLT
  //   SLTU
  //   XOR
  //   SRL
  //   SRA
  //   OR
  //   AND
  //   bit 5 of funct7 is used a lot
  //   on if rs1 < rs2
endmodule

module immediate_chooser (
  input  [6:0] opcode,
  input  [2:0] funct3,
  output I,
  output R,
  output S,
  output B,
  output U,
  output J
);

  wire comparator_1_eq, comparator_2_eq, comparator_3_eq, comparator_4_eq, comparator_5_eq, comparator_6_eq,
       comparator_9_eq, comparator_10_eq, demultiplexer_1_out0, demultiplexer_1_out1, or_1_out;

  Comparator #(.width(3)) comparator_1 (.a(funct3), .b(3'b001), .eq(comparator_1_eq));  // open: gt, lt
  Comparator #(.width(3)) comparator_2 (.a(funct3), .b(3'b101), .eq(comparator_2_eq));  // open: gt, lt
  or or_1 (or_1_out, comparator_1_eq, comparator_2_eq);
  Comparator #(.width(5)) comparator_3 (.a(opcode[6:2]), .b({5{1'b0}}), .eq(comparator_3_eq));  // open: gt, lt
  Demultiplexer demultiplexer_1 (
    .out0(demultiplexer_1_out0), .out1(demultiplexer_1_out1), .in(comparator_4_eq), .sel(or_1_out));  // open: en
  Comparator #(.width(5)) comparator_4 (.a(opcode[6:2]), .b(5'b00100), .eq(comparator_4_eq));  // open: gt, lt
  Comparator #(.width(5)) comparator_5 (.a(opcode[6:2]), .b(5'b11001), .eq(comparator_5_eq));  // open: gt, lt
  Comparator #(.width(5)) comparator_6 (.a(opcode[6:2]), .b(5'b01100), .eq(comparator_6_eq));  // open: gt, lt
  Comparator #(.width(5)) comparator_7 (.a(opcode[6:2]), .b(5'b01000), .eq(S));  // open: gt, lt
  Comparator #(.width(5)) comparator_8 (.a(opcode[6:2]), .b(5'b11000), .eq(B));  // open: gt, lt
  Comparator #(.width(5)) comparator_9 (.a(opcode[6:2]), .b(5'b01101), .eq(comparator_9_eq));  // open: gt, lt
  Comparator #(.width(5)) comparator_10 (.a(opcode[6:2]), .b(5'b00101), .eq(comparator_10_eq));  // open: gt, lt
  Comparator #(.width(5)) comparator_11 (.a(opcode[6:2]), .b(5'b11011), .eq(J));  // open: gt, lt
  or or_2 (I, comparator_3_eq, demultiplexer_1_out0, comparator_5_eq);
  or or_3 (R, demultiplexer_1_out1, comparator_6_eq);
  or or_4 (U, comparator_9_eq, comparator_10_eq);
endmodule

module branch_evaluator (
  input  [31:0] rs1,
  input  [31:0] rs2,
  input  [2:0] funct3,
  output out_4
);

  wire comparator_1_eq, comparator_1_lt, comparator_2_gt, multiplexer_1_out, undriven;

  Comparator #(.width(32)) comparator_1 (.a(rs1), .b(rs2), .eq(comparator_1_eq), .lt(comparator_1_lt));  // open: gt
  Comparator #(.width(32), .mode("unsigned")) comparator_2 (.a(rs2), .b(rs1), .gt(comparator_2_gt));  // open: eq, lt
  Multiplexer #(.select(2)) multiplexer_1 (
    .in0(comparator_1_eq), .in1(comparator_1_lt), .in2(comparator_1_lt), .in3(comparator_2_gt),
    .out(multiplexer_1_out), .sel(funct3[2:1]), .en(undriven));
  xor xor_1 (out_4, multiplexer_1_out, funct3[0]);

  // Notes on the sheet:
  //   NOTE: 010 and 011 are invalid funct3 values for branch. they are treated as if they were 100 and 101
  //   least significant bit of funct3 inverts branch
endmodule

module LUI_AUIPC_JAL_JALR (
  input  [6:0] in_1,
  output JALR,
  output JAL,
  output AUIPC,
  output LUI
);

  Comparator #(.width(7)) comparator_1 (.a(7'b1100111), .b(in_1), .eq(JALR));  // open: gt, lt
  Comparator #(.width(7)) comparator_2 (.a(7'b1101111), .b(in_1), .eq(JAL));  // open: gt, lt
  Comparator #(.width(7)) comparator_3 (.a(7'b0010111), .b(in_1), .eq(AUIPC));  // open: gt, lt
  Comparator #(.width(7)) comparator_4 (.a(7'b0110111), .b(in_1), .eq(LUI));  // open: gt, lt
endmodule
